# Fritzing sketch v1 (saved by Fritzing 0.9.3b)
circuit board: 5.47562cm x 3.28104cm
perfboards: 1

parts:
  J1 = female pin header, 2 pins [form="♀ (female)"]
  J2 = female pin header, 2 pins [form="♀ (female)"]
  J4 = female pin header, 2 pins [form="♀ (female)"]
  J5 = female pin header, 2 pins [form="♀ (female)"]
  J6 = female pin header, 2 pins [form="♀ (female)"]
  S1 = Pushbutton [package="[THT]"]
  J3 = female pin header, 2 pins [form="♀ (female)"]
  S2 = Pushbutton [package="[THT]"]
  R1 = Resistor [tolerance=±5% resistance=10k package=THT]
  R2 = Resistor [tolerance=±5% resistance=10k package=THT]
  J7 = female pin header, 2 pins [form="♀ (female)"]

nets:
  N1: J1.pin1, R1.Pin_0
  N2: J1.pin2, J6.pin2
  N3: J2.pin1, J4.pin1
  N4: J4.pin2, R1.Pin_1
  N5: J5.pin1, J3.pin1, S2.Pin_1, S2.Pin_2, S2.Pin_3, S2.Pin_4, R2.Pin_0, J7.pin1
  N6: J6.pin1, S1.Pin_1, S1.Pin_2
  N7: S1.Pin_3, S1.Pin_4, R2.Pin_1
